# Fritzing sketch arduino (saved by Fritzing 0.9.2b)
breadboards: 1

parts:
  Servo = Arduino Nano (Rev3.0)
  J1 = Basic Servo
  FSR = Basic Force Sensing Resistor (FSR) [package=THT]
  R1 = Resistor [tolerance=±5% resistance=1.2k package="2010 [SMD]"]

nets:
  GND: Servo.GND, J1.gnd, R1.Pin_1
  N1: Servo.D12/MISO, J1.pulse
  5V: Servo.5V, J1.vcc, FSR.pin_0
  N2: Servo.A1, FSR.pin_1, R1.Pin_0
